# Fritzing sketch sketch (saved by Fritzing 0.9.3b)
breadboards: 1

parts:
  R1 = Resistor [tolerance=±5% resistance=220 package=THT]
  Part1 = Arduino Motor Shield (Rev3)
  R2 = Resistor [tolerance=±5% resistance=220 package=THT]
  C1 = Tantalum Capacitor [capacitance=1μF package="100 mil [THT, tantalum]"]
  C2 = Tantalum Capacitor [capacitance=1μF package="100 mil [THT, tantalum]"]
  J1 = Piezo Speaker
  U1 = GAS_SENSOR [package=mq-3]  # not connected
  S1 = Toggle Switch [package=THT]
  S2 = Toggle Switch [package=THT]

nets:
  N1: R1.Pin_0, C2.+
  N2: R1.Pin_1, Part1.D4
  N3: Part1.GND, C1.+, C2.-, J1.pin1, S1.L1
  N4: Part1.A5, S2.L2
  N5: Part1.D2, J1.pin2
  N6: Part1.D5_PWM, R2.Pin_0
  N7: Part1.5V, S2.L1
  N8: R2.Pin_1, C1.-
